# Fritzing sketch rv_schematic (saved by Fritzing 0.9.3b)
breadboards: 1

parts:
  U1 = 16-Channel Relay Module [package=relay-16ch]
  Bauteil1 = BluePill
  TM1638_Led_and_Key1 = TM1638_Led_and_Key [package=THT]
  TM1638_Led_and_Key2 = TM1638_Led_and_Key [package=THT]
  U2 = MCP23017 [package="DIP (Dual Inline) [THT]"]
  R1 = Resistor [tolerance=±5% resistance=2.2k package=THT]
  R2 = Resistor [tolerance=±5% resistance=2.2k package=THT]

nets (from the schematic view):
  N1: U1.IN1, U2.GPA0
  N2: U1.IN2, U2.GPA1
  N3: U1.IN3, U2.GPA2
  N4: U1.IN4, U2.GPA3
  N5: U1.IN5, U2.GPA4
  N6: U1.IN6, U2.GPA5
  N7: U1.IN7, U2.GPA6
  N8: U1.IN8, U2.GPA7
  N9: U1.IN9, U2.GPB0
  N10: U1.IN10, U2.GPB1
  N11: U1.IN11, U2.GPB2
  N12: U1.IN12, U2.GPB3
  N13: U1.IN13, U2.GPB4
  N14: U1.IN14, U2.GPB5
  N15: U1.IN15, U2.GPB6
  N16: U1.IN16, U2.GPB7
  N17: U1.VCCOUT_5V, Bauteil1.5V, R1.Pin_1, R2.Pin_1
  N18: Bauteil1.B10, U2.SCL, R1.Pin_0
  N19: Bauteil1.B11, U2.SDA, R2.Pin_0
  N20: Bauteil1.B15, TM1638_Led_and_Key1.STB
  N21: Bauteil1.B12, TM1638_Led_and_Key2.STB
  N22: U2.A1, U2.A2

custom parts:
  16-Channel Relay Module: 16 channel relay module
  MCP23017: 16 bit I/O chip controlled via I2C
